# Fritzing sketch project (saved by Fritzing 0.9.3b)
breadboards: 1

parts:
  Componente1 = Arduino Uno (Rev3)
  7_Segment1 = 7-Segment LED Display [package=THT]
  7_Segment2 = 7-Segment LED Display [package=THT]
  R1 = Resistor [tolerance=±5% resistance=220 package=THT]
  R2 = Resistor [tolerance=±5% resistance=220 package=THT]
  T1 = LM35 Temperature Sensor [package="TO92 [THT]"]
  M1 = DC Motor

nets:
  N1: Componente1.A0, T1.Vout
  N2: Componente1.D8, 7_Segment2.cathodeB
  N3: Componente1.D9_PWM, 7_Segment2.cathodeC
  N4: Componente1.D10_PWM/SS, 7_Segment2.commAnode#2
  N5: Componente1.D11_PWM/MOSI, 7_Segment2.cathodeD
  N6: Componente1.D12/MISO, 7_Segment2.commAnode#7
  N7: Componente1.D13/SCK, 7_Segment2.cathodeF
  GND: Componente1.GND, R1.Pin_1, R2.Pin_1, T1.GND
  N8: Componente1.D0/RX, 7_Segment1.cathodeA
  N9: Componente1.D1/TX, 7_Segment1.cathodeB
  N10: Componente1.D2, 7_Segment1.cathodeC
  N11: Componente1.D3_PWM, 7_Segment1.cathodeD
  N12: Componente1.D4, 7_Segment1.cathodeE
  N13: Componente1.D5_PWM, 7_Segment1.commAnode#7
  N14: Componente1.D6_PWM, 7_Segment1.commAnode#2
  N15: Componente1.D7, 7_Segment2.cathodeA
  N16: Componente1.5V, T1.+Vs
  N17: 7_Segment1.cathodeF, R1.Pin_0
  N18: 7_Segment1.cathodeG, R2.Pin_0
  N19: M1.pin_1, M1.pin_2
